# Fritzing sketch spicerack (saved by Fritzing 0.9.3b)
breadboards: 1

parts:
  BeagleBone1 = BeagleBone Black
  J1 = Basic Servo  # not connected
  VCC1 = Battery block 9V  # not connected
  Part1 = EasyDriver_v44
  M1 = Stepper Motor - Bipolar

nets:
  N1: BeagleBone1.no_name_yet#102, Part1.GND
  N2: BeagleBone1.no_name_yet#108, Part1.ENABLE
  N3: BeagleBone1.no_name_yet#110, Part1.MS2
  N4: BeagleBone1.no_name_yet#112, Part1.MS1
  N5: BeagleBone1.no_name_yet#114, Part1.STEP
  N6: BeagleBone1.no_name_yet#116, Part1.DIR
  N7: Part1.OUT2A, M1.A
  N8: Part1.OUT2B, M1.C
  N9: Part1.OUT1A, M1.B
  N10: Part1.OUT1B, M1.D

custom parts:
  BeagleBone Black: BeagleBone Black rev. A5B
